# Fritzing sketch main (saved by Fritzing 0.9.6b)
breadboards: 1

parts:
  PIC_16F877A1 = PIC 16F877A [package=THT]
  R1 = Resistor [tolerance=±5% power=0.25 resistance=220 package=THT]
  LED1 = LED - 5mm [color="Blue (430nm)" current=0.030 package="5 mm [THT]"]
  S1 = Pushbutton [package="[THT]"]
  R2 = Resistor [tolerance=±5% power=0.25 resistance=1k package=THT]

nets:
  N1: PIC_16F877A1.RA0/AN0, PIC_16F877A1.VDD#31, S1.Pin_1, S1.Pin_2, S1.Pin_3, S1.Pin_4, R2.Pin_0
  N2: PIC_16F877A1.VSS#30, R1.Pin_1, R2.Pin_1
  N3: PIC_16F877A1.RB0/INT, LED1.anode
  N4: R1.Pin_0, LED1.cathode
